# Fritzing sketch Untitled Sketch 2 (saved by Fritzing 0.9.2b)
breadboards: 1

parts:
  U1 = NodeMCU V3.0
  LED1 = smd LED [color="Yellow (585nm)" package="0805 [SMD]"]
  R1 = Resistor [tolerance=±5% resistance=470 package="0603 [SMD]"]
  LED2 = smd LED [color="Green (555nm)" package="0805 [SMD]"]
  R2 = Resistor [tolerance=±5% resistance=470 package="0603 [SMD]"]
  LED3 = smd LED [color="Infrared (850nm)" package="0805 [SMD]"]
  Q1 = TRANSISTOR_PNP [package=to-92]
  R3 = Resistor [tolerance=±5% resistance=470 package="0603 [SMD]"]
  DHT1 = DHT22 Humidity and Temperature Sensor
  R4 = Resistor [tolerance=±5% resistance=10k package="0603 [SMD]"]

nets:
  VIN: U1.D4, U1.Vin, DHT1.VDD, DHT1.DATA, R4.Pin_0
  N1: U1.3V3, R2.Pin_1, LED3.anode
  N2: U1.GND#6, U1.GND#13, U1.GND#16, U1.GND#33, LED1.cathode, LED2.cathode, Q1.E, DHT1.GND
  N3: U1.RX, R3.Pin_1
  N4: LED1.anode, R1.Pin_0
  N5: LED2.anode, R2.Pin_0
  N6: LED3.cathode, Q1.C
  N7: Q1.B, R3.Pin_0

custom parts:
  NodeMCU V3.0: ESP8266 based NodeMCU
